// Logisim project cpu.circ as structural Verilog
module main (
  input  [15:0] INSTRUCTION,
  input  CLOCK,
  output [15:0] FETCH_ADDRESS,
  output Overflow,
  output [15:0] s0_Value,
  output [15:0] s1_Value,
  output [15:0] s2_Value,
  output [15:0] ra_Value,
  output [15:0] sp_Value,
  output [15:0] HI_Value,
  output [15:0] LO_Value
);

  wire MEM_p1, MEM_p3, MEM_p6, MEM_p9, MEM_p12;

  Register #(.width(16)) PC ();  // open: D, en, Q, clk, clr
  Register #(.width(16)) LO ();  // open: D, en, Q, clk, clr
  Register #(.width(16)) HI ();  // open: D, en, Q, clk, clr
  // regfile_main main_1: pin names not known
  // alu_main main_2: pin names not known
  // mem_main MEM: pin names not known; wires that end beside it: MEM_p1, s0_Value, MEM_p3, MEM_p3, s1_Value, MEM_p6, MEM_p6, s2_Value, MEM_p9, MEM_p9, ra_Value, MEM_p12, MEM_p12, sp_Value

  // Other names for the same wires on the sheet: clk = CLOCK; fetch_addr[15:0] = FETCH_ADDRESS

  // Notes on the sheet:
  //   Output
  //   These are outputs/inputs from run.circ
  //   Inputs
  //   These are DEBUG/TEST outputs from your circuit.
endmodule

module Control_signal (
  input  [15:0] Input,
  output RegWr,
  output Jump,
  output Branch,
  output ExtOp,
  output AluSrc,
  output MemWrite,
  output MemToReg,
  output [2:0] AluCtr
);

  wire addi, addiu, andi, beq, bne, j, jr, lh, lui, mfhi, mflo, or_4_out, ori, R, slti;
  wire [2:0] AluCtr_not_R;

  Multiplexer #(.select(4), .width(3)) multiplexer_1 (
    .in6(3'b010), .in7(3'b101), .in8(3'b110), .in9(3'b011), .in10(3'b100), .out(AluCtr_not_R),
    .sel(Input[15:12]));  // open: in0, in1, in2, in3, in4, in5, in11, in12, in13, in14, in15, en
  and isRtype (R, ~Input[12], ~Input[13], ~Input[14], ~Input[15]);  // AND_Gate
  and and_1 (lui, Input[12], ~Input[13], ~Input[14], ~Input[15]);  // AND_Gate
  and and_2 (beq, ~Input[15], Input[14], ~Input[13], ~Input[12]);  // AND_Gate
  and and_3 (j, ~Input[15], ~Input[14], Input[13], ~Input[12]);  // AND_Gate
  and and_4 (addi, ~Input[15], Input[14], Input[13], ~Input[12]);  // AND_Gate
  and and_5 (addiu, ~Input[15], Input[14], Input[13], Input[12]);  // AND_Gate
  and and_6 (slti, Input[15], ~Input[14], ~Input[13], ~Input[13]);  // AND_Gate
  and and_7 (mfhi, Input[15], Input[14], ~Input[13], Input[12]);  // AND_Gate
  and and_8 (mflo, Input[15], Input[14], Input[13], ~Input[12]);  // AND_Gate
  and and_9 (andi, Input[15], ~Input[14], ~Input[13], Input[12]);  // AND_Gate
  and and_10 (ori, Input[15], ~Input[14], Input[13], ~Input[12]);  // AND_Gate
  and and_11 (lh, Input[15], ~Input[14], Input[13], Input[12]);  // AND_Gate
  and and_12 (MemWrite, Input[15], Input[14], ~Input[13], ~Input[12]);  // AND_Gate
  and and_13 (bne, ~Input[15], Input[14], ~Input[13], Input[12]);  // AND_Gate
  and and_14 (jr, ~Input[15], ~Input[14], Input[13], Input[13]);  // AND_Gate
  Multiplexer #(.width(3)) multiplexer_2 (.in0(AluCtr_not_R), .in1(Input[2:0]), .out(AluCtr), .sel(R));  // open: en
  or or_1 (RegWr, R, lui, addi, addiu, mfhi, mflo, ori, lh);
  or or_2 (Jump, j, jr);
  or or_3 (Branch, beq, bne);
  or or_4 (or_4_out, andi, ori);
  not not_1 (ExtOp, or_4_out);
  or or_5 (AluSrc, addi, ori, lh, andi, MemWrite, addiu);
  or or_6 (MemToReg, mflo, mfhi, lh);

  // Other names for the same wires on the sheet: sh = MemWrite

  // Notes on the sheet:
  //   sll
  //   addi
  //   and
  //   or
  //   addiu
  //   slti
endmodule
